# Fritzing sketch Conexionado_telemetría (saved by Fritzing 0.9.4)
circuit board: 8.46667cm x 5.64444cm

parts:
  U1 = NodeMCU V3.0
  RFM1 = RFM69HCW ISM Transciever
  ANT1 = Antenna
  J1 = STARBOARD_GND [package=starboard_ground_wide]
  C1 = Capacitor Polarized [part_number=47uF package=cpol-radial-10uf-25v]

nets:
  N1: U1.3V3, RFM1.13_3.3V, C1.+
  N2: U1.D5, RFM1.4_SCK
  N3: U1.D6, RFM1.2_MISO
  N4: U1.D7, RFM1.3_MOSI
  N5: U1.D8, RFM1.5_NSS_(CS)
  N6: U1.GND, RFM1.8_GND, C1.-
  N7: U1.S3, RFM1.14_DIO0
  N8: RFM1.9_ANT, ANT1.antenna_lead
  N9: RFM1.10_GND, J1.MOUNT

notes:
  MISO → Amarillo → D6
  MOSI → Verde → D7
  SCK → Amarillo-Rojo → D5
  NSS → Marrón-Amarillo → D8
  DIO0 → Marrón-Verde → D1 ¿D2?
  POSIBLE DIO0 --> GPIO10 (SDD3)
  GND → Negro → condensador de 47uF (-)
  3.3V → Rojo → condensador de 47uF (+)
  Antena y GND → Conector
  Importante: la antena SIEMPRE conectada
  La lógica del RFM69HCW es siempre a 3.3V. Si se usa componentes con 5V, hay que poner un shift level.
  Importante: con NodeMCU, necesario condensador de 47uF entre
  3.3V y GND
  // Based on RFM69 library sample code by Felix Rusu
  // http://LowPowerLab.com/conSerial.println("probando...");tact
  Puede ser GPIO10, o D1 u otro que no afecte a la carga ¿D2?

custom parts:
  NodeMCU V3.0: ESP8266 based NodeMCU
  RFM69HCW ISM Transciever: RF Transceiver by Hope RF. Well supported Arduino libraries are available. This ISM band transceiver is available in several frequencies e.g. 433MHz and 915MHz and it is also available in various feature versions.
